// Logisim project t888.circ as structural Verilog: 7 circuits, main circuit t888
module t888 (
);

  wire bru_1_loopz;
  wire [1:0] alu_1_state;
  wire [4:0] iou_1_ram_control;
  wire [7:0] alu_1_r_bus, bru_1_a_bus, bru_1_b_bus, bru_1_instruction, bru_1_ramaddr, bru_1_rom_address,
       idu_1_iou, rom_1_data;
  wire [9:0] idu_1_alu;
  wire [19:0] idu_1_bru;

  ROM #(.Select("low")) rom_1 (.addr(bru_1_rom_address), .data(rom_1_data));
  BRU bru_1 (
    .ROM_Data(rom_1_data), .instruction(bru_1_instruction), .R_Bus(alu_1_r_bus), .A_Bus(bru_1_a_bus),
    .ROM_Address(bru_1_rom_address), .loopz(bru_1_loopz), .B_Bus(bru_1_b_bus), .RAMAddr(bru_1_ramaddr),
    .control(idu_1_bru));
  ALU alu_1 (.B_Bus(bru_1_b_bus), .R_Bus(alu_1_r_bus), .State(alu_1_state), .Control(idu_1_alu), .A_Bus(bru_1_a_bus));
  IDU idu_1 (
    .Instr(bru_1_instruction), .loopz(bru_1_loopz), .ALU_state(alu_1_state), .BRU(idu_1_bru),
    .ALU(idu_1_alu), .IOU(idu_1_iou));
  IOU iou_1 (
    .Address(bru_1_ramaddr), .Store_Bus(alu_1_r_bus), .Control(idu_1_iou), .Load_Bus(bru_1_b_bus),
    .RAM_control(iou_1_ram_control));
  RAM #(.bus("separate"), .Select("low")) ram_1 (
    .addr(bru_1_ramaddr), .din(alu_1_r_bus), .data(bru_1_b_bus), .str(iou_1_ram_control[0]),
    .sel(iou_1_ram_control[1]), .clk(iou_1_ram_control[2]), .ld(iou_1_ram_control[3]),
    .clr(iou_1_ram_control[4]));
endmodule

module ALU (
  input  [7:0] B_Bus,
  input  [7:0] A_Bus,
  input  [9:0] Control,
  output [7:0] R_Bus,
  output [1:0] State
);

  wire adder_2_cout, C_en_q, multiplexer_2_out, not_2_out, subtractor_2_bout, subtractor_3_bout, undriven,
       zerotest_1_iszero;
  wire [0:0] and_2_out;
  wire [7:0] adder_1_out, adder_2_out, and_1_out, multiplexer_1_out, multiplexer_3_out, negator_1_out,
       not_1_out, or_1_out, subtractor_1_out, subtractor_2_out, subtractor_3_out, xor_1_out;

  Adder adder_1 (.a(A_Bus), .b(8'h1), .out(adder_1_out));  // open: cin, cout
  Subtractor subtractor_1 (.a(A_Bus), .b(8'h1), .out(subtractor_1_out));  // open: bin, bout
  Negator negator_1 (.in(A_Bus), .out(negator_1_out));
  assign not_1_out = ~A_Bus;  // NOT_Gate not_1, 8 bits wide
  Multiplexer #(.width(8), .enable("false")) multiplexer_1 (
    .in0(B_Bus), .in1(A_Bus), .out(multiplexer_1_out), .sel(undriven));
  Adder adder_2 (.a(A_Bus), .b(B_Bus), .out(adder_2_out), .cin(and_2_out[0]), .cout(adder_2_cout));
  Subtractor subtractor_2 (.a(A_Bus), .b(B_Bus), .out(subtractor_2_out), .bin(and_2_out[0]), .bout(subtractor_2_bout));
  Subtractor subtractor_3 (.a(B_Bus), .b(A_Bus), .out(subtractor_3_out), .bin(and_2_out[0]), .bout(subtractor_3_bout));
  assign and_1_out = A_Bus & B_Bus;  // AND_Gate and_1, 8 bits wide
  assign or_1_out = A_Bus | B_Bus;  // OR_Gate or_1, 8 bits wide
  assign xor_1_out = A_Bus ^ B_Bus;  // XOR_Gate xor_1, 8 bits wide
  not not_2 (not_2_out, Control[8]);
  Register #(.width(1), .Select("high")) C_en (
    .D(Control[5]), .en(Control[4]), .Q(C_en_q), .clk(Control[0]), .clr(Control[1]));
  Multiplexer #(.select(3)) multiplexer_2 (
    .in1(adder_2_cout), .in2(subtractor_2_bout), .in3(subtractor_3_bout), .in5(A_Bus[7]), .in6(A_Bus[0]),
    .in7(A_Bus[0]), .out(multiplexer_2_out), .sel({Control[9], Control[7:6]}), .en(not_2_out));  // open: in0, in4
  and and_2 (and_2_out[0], C_en_q, State[1]);
  Register #(.width(1), .Select("high")) Carry (
    .D(multiplexer_2_out), .en(Control[2]), .Q(State[1]), .clk(Control[0]), .clr(Control[4]));
  Multiplexer #(.select(4), .width(8), .enable("false")) multiplexer_3 (
    .in0({8{1'b0}}), .in1({A_Bus[6:0], and_2_out[0]}), .in2({and_2_out[0], A_Bus[7:1]}),
    .in3({{2{A_Bus[7]}}, A_Bus[6:1]}), .in4(adder_1_out), .in5(subtractor_1_out), .in6(negator_1_out),
    .in7(not_1_out), .in8(multiplexer_1_out), .in9(adder_2_out), .in10(subtractor_2_out),
    .in11(subtractor_3_out), .in12(and_1_out), .in13(or_1_out), .in14(xor_1_out), .in15(A_Bus),
    .out(multiplexer_3_out), .sel(Control[9:6]));
  assign R_Bus = Control[3] ? multiplexer_3_out : 8'bz;  // Controlled_Buffer controlled_buffer_1
  ZeroTest zerotest_1 (.Input(multiplexer_3_out), .IsZero(zerotest_1_iszero));
  Register #(.width(1), .Select("high")) Zero (
    .D(zerotest_1_iszero), .en(Control[2]), .Q(State[0]), .clk(Control[0]), .clr(Control[1]));

  // Other names for the same wires on the sheet: clock = Control[0]; reset = Control[1]; Z_enable = Control[2];
  //   output_enable = Control[3]; set_carry_mode_and_clear_carry = Control[4]; enable_carry_in = Control[5];
  //   op_select[3:0] = Control[9:6]

  // Notes on the sheet:
  //   B_Bus: pull=down
  //   A_Bus: pull=down
  //   Control: pull=down
endmodule

module ZeroTest (
  input  [7:0] Input,
  output IsZero
);

  nor nor_1 (IsZero, Input[0], Input[1], Input[2], Input[3], Input[4], Input[5], Input[6], Input[7]);

  // Notes on the sheet:
  //   Input: pull=up
endmodule

module BRU (
  input  [7:0] R_Bus,
  input  [7:0] ROM_Data,
  input  [19:0] control,
  output [7:0] instruction,
  output [7:0] A_Bus,
  output [7:0] RAMAddr,
  output [7:0] B_Bus,
  output loopz,
  output [7:0] ROM_Address
);

  wire undriven;
  wire [5:0] offset_q;
  wire [7:0] accum_q, bit_extender_1_out, loop_q, multiplexer_1_out, point_q, sp_1_pointer;

  Multiplexer #(.width(8), .enable("false")) multiplexer_1 (
    .in0(R_Bus), .in1(ROM_Data), .out(multiplexer_1_out), .sel(control[10]));
  Register #(.trigger("high"), .Select("low")) inst (
    .D(multiplexer_1_out), .en(control[11]), .Q(instruction), .clk(control[12]), .clr(control[13]));
  Register #(.Select("low")) accum (
    .D(multiplexer_1_out), .en(control[9]), .Q(accum_q), .clk(control[12]), .clr(control[13]));
  assign bit_extender_1_out = {{2{ROM_Data[5]}}, ROM_Data[5:0]};  // Bit_Extender bit_extender_1
  Multiplexer #(.width(8), .enable("false")) multiplexer_2 (
    .in0(accum_q), .in1(bit_extender_1_out), .out(A_Bus), .sel(control[14]));
  SP sp_1 (.en(control[8]), .push_pop(control[7]), .pointer(sp_1_pointer), .clk(control[12]), .clr(control[13]));
  Counter #(.behavior("old")) point (
    .load(control[5]), .D(multiplexer_1_out), .count(control[6]), .Q(point_q), .clk(control[12]),
    .clr(control[13]), .preset(undriven));  // open: carry
  Multiplexer #(.select(2), .width(8), .enable("false")) multiplexer_3 (
    .in0(ROM_Data), .in1(sp_1_pointer), .in2(point_q), .in3({offset_q, ROM_Data[1:0]}), .out(RAMAddr),
    .sel(control[16:15]));
  Register #(.width(6), .Select("low")) offset (
    .D(multiplexer_1_out[5:0]), .en(control[4]), .Q(offset_q), .clk(control[12]), .clr(control[13]));
  Multiplexer #(.select(3), .width(8), .enable("false")) multiplexer_4 (
    .in1(accum_q), .in2({2'b00, offset_q}), .in3(point_q), .in4(ROM_Data), .in5(loop_q), .in6(ROM_Address),
    .out(B_Bus), .sel(control[19:17]));  // open: in0, in7
  Counter #(.ongoal("stay"), .behavior("old")) loop (
    .load(control[2]), .D(multiplexer_1_out), .count(control[3]), .Q(loop_q), .carry(loopz),
    .clk(control[12]), .clr(control[13]));  // open: preset
  Counter #(.behavior("old")) prog (
    .load(control[0]), .D(multiplexer_1_out), .count(control[1]), .Q(ROM_Address), .clk(control[12]),
    .clr(control[13]));  // open: carry, preset

  // Notes on the sheet:
  //   rjump
  //   stack
endmodule

module SP (
  input  en,
  input  push_pop,
  input  clk,
  input  clr,
  output [7:0] pointer
);

  wire [7:0] adder_1_out, multiplexer_1_out, register_1_q;

  Register #(.Select("low")) register_1 (.D(adder_1_out), .en(en), .Q(register_1_q), .clk(clk), .clr(clr));
  Multiplexer #(.width(8), .enable("false")) multiplexer_1 (
    .in0({8{1'b1}}), .in1(8'h1), .out(multiplexer_1_out), .sel(push_pop));
  Adder adder_1 (.a(multiplexer_1_out), .b(register_1_q), .out(adder_1_out));  // open: cin, cout
  Multiplexer #(.width(8), .enable("false")) multiplexer_2 (
    .in0(adder_1_out), .in1(register_1_q), .out(pointer), .sel(push_pop));

  // Notes on the sheet:
  //   Stack Pointer
  //   stack grows downward from 0xFF
endmodule

module IDU (
  input  [7:0] Instr,
  input  loopz,
  input  [1:0] ALU_state,
  output [19:0] BRU,
  output [9:0] ALU,
  output [7:0] IOU
);
endmodule

module IOU (
  input  [7:0] Address,
  input  [7:0] Store_Bus,
  input  [7:0] Control,
  output [7:0] Load_Bus,
  output [4:0] RAM_control
);
endmodule
